// Digital circuit hw3_1.dig as structural Verilog
module hw3_1 (
  input  adder_substractor,
  input  in_2,
  input  in_3,
  input  in_4,
  input  in_5,
  input  in_6,
  input  in_7,
  input  in_8,
  input  in_9
);

  wire add_1_c_o, add_1_s, add_2_c_o, add_2_s, add_3_c_o, add_3_s, sub_1_c_o, sub_1_s, xor_1_out, xor_2_out,
       xor_3_out, xor_4_out;

  xor xor_1 (xor_1_out, adder_substractor, in_3);
  xor xor_2 (xor_2_out, adder_substractor, in_5);
  xor xor_3 (xor_3_out, adder_substractor, in_8);
  xor xor_4 (xor_4_out, adder_substractor, in_9);
  Add add_1 (.a(in_2), .b(xor_1_out), .c_i(1'b0), .s(add_1_s), .c_o(add_1_c_o));
  Add add_2 (.a(in_4), .b(xor_2_out), .c_i(add_1_c_o), .s(add_2_s), .c_o(add_2_c_o));
  Add add_3 (.a(in_6), .b(xor_3_out), .c_i(add_2_c_o), .s(add_3_s), .c_o(add_3_c_o));
  Sub sub_1 (.a(in_7), .b(xor_4_out), .c_i(add_3_c_o), .s(sub_1_s), .c_o(sub_1_c_o));
  LED led_1 (.in(add_1_s));
  LED led_2 (.in(sub_1_c_o));
  LED led_3 (.in(add_2_s));
  LED led_4 (.in(add_3_s));
  LED led_5 (.in(sub_1_s));
endmodule
