// Digital circuit hw3_6.dig as structural Verilog
module hw3_6 (
  input  up_down,
  input  Vcc,
  input  CLK
);

  wire and_1_out, and_2_out, and_3_out, and_4_out, d_ff_1_nq, d_ff_1_q, d_ff_2_nq, d_ff_2_q, not_1_out,
       or_1_out, or_2_out;

  not not_1 (not_1_out, up_down);
  D_FF d_ff_1 (.D(Vcc), .C(CLK), .Q(d_ff_1_q), .nQ(d_ff_1_nq));
  and and_1 (and_1_out, not_1_out, d_ff_1_q);
  and and_2 (and_2_out, up_down, d_ff_1_nq);
  or or_1 (or_1_out, and_1_out, and_2_out);
  D_FF d_ff_2 (.D(Vcc), .C(or_1_out), .Q(d_ff_2_q), .nQ(d_ff_2_nq));
  and and_3 (and_3_out, not_1_out, d_ff_2_q);
  and and_4 (and_4_out, up_down, d_ff_2_nq);
  or or_2 (or_2_out, and_3_out, and_4_out);
  D_FF d_ff_3 (.D(Vcc), .C(or_2_out));  // open: Q, nQ
endmodule
