// Digital circuit idkwhatthisis.dig as structural Verilog
module idkwhatthisis (
  input  in_1
);

  wire A0_out, A1_out, A2_out, and_1_out, and_2_out, and_3_out, and_4_out, and_5_out, and_6_out, and_7_out,
       and_8_out, and_9_out, B0_out, B1_out, B2_out, or_1_out, or_2_out, or_3_out, or_4_out, or_5_out,
       or_6_out, xor_1_out, xor_2_out, xor_3_out, xor_4_out, xor_5_out, xor_6_out;

  DipSwitch A0 (.out(A0_out));
  DipSwitch B0 (.out(B0_out));
  DipSwitch A1 (.out(A1_out));
  DipSwitch B1 (.out(B1_out));
  DipSwitch A2 (.out(A2_out));
  DipSwitch B2 (.out(B2_out));
  xor xor_1 (xor_1_out, A0_out, B0_out);
  and and_1 (and_1_out, A0_out, B0_out);
  and and_2 (and_2_out, A0_out, in_1);
  and and_3 (and_3_out, B0_out, in_1);
  xor xor_2 (xor_2_out, A1_out, B1_out);
  and and_4 (and_4_out, A1_out, B1_out);
  and and_5 (and_5_out, A1_out, or_4_out);
  and and_6 (and_6_out, B1_out, or_4_out);
  xor xor_3 (xor_3_out, A2_out, B2_out);
  and and_7 (and_7_out, A2_out, B2_out);
  and and_8 (and_8_out, A2_out, or_5_out);
  and and_9 (and_9_out, B2_out, or_5_out);
  or or_1 (or_1_out, and_1_out, and_2_out);
  or or_2 (or_2_out, and_4_out, and_5_out);
  or or_3 (or_3_out, and_7_out, and_8_out);
  xor xor_4 (xor_4_out, in_1, xor_1_out);
  xor xor_5 (xor_5_out, or_4_out, xor_2_out);
  xor xor_6 (xor_6_out, or_5_out, xor_3_out);
  or or_4 (or_4_out, or_1_out, and_3_out);
  or or_5 (or_5_out, or_2_out, and_6_out);
  or or_6 (or_6_out, or_3_out, and_9_out);
  Seven_Seg seven_seg_1 ();  // open: a, b, c, d, e, f, g, dp
  LED led_1 (.in(xor_6_out));
endmodule
