// Digital circuit lab2.dig as structural Verilog
module lab2 (
  input  in_1
);

  wire A0_out, A1_out, A2_out, A3_out, add_1_c_o, add_1_s, add_2_c_o, add_2_s, add_3_c_o, add_3_s, add_4_c_o,
       add_4_s, and_1_out, and_2_out, and_3_out, and_4_out, and_5_out, and_6_out, and_7_out, and_8_out,
       and_9_out, and_10_out, and_11_out, and_12_out, and_13_out, and_14_out, and_15_out, and_16_out,
       and_17_out, and_18_out, B0_out, B1_out, B2_out, B3_out, not_1_out, not_2_out, not_3_out, not_4_out,
       not_5_out, not_6_out, not_7_out, not_8_out, not_9_out, not_10_out, not_11_out, not_12_out, not_13_out,
       not_14_out, not_15_out, not_16_out, not_17_out, not_18_out, not_19_out, not_20_out, not_21_out,
       not_22_out, not_23_out, not_24_out, or_1_out, or_2_out, or_3_out, or_4_out, or_5_out, or_6_out,
       or_7_out;

  DipSwitch A0 (.out(A0_out));
  DipSwitch B0 (.out(B0_out));
  DipSwitch A1 (.out(A1_out));
  DipSwitch B1 (.out(B1_out));
  DipSwitch A2 (.out(A2_out));
  DipSwitch B2 (.out(B2_out));
  DipSwitch A3 (.out(A3_out));
  DipSwitch B3 (.out(B3_out));
  Add add_1 (.a(A0_out), .b(B0_out), .c_i(in_1), .s(add_1_s), .c_o(add_1_c_o));
  Add add_2 (.a(A1_out), .b(B1_out), .c_i(add_1_c_o), .s(add_2_s), .c_o(add_2_c_o));
  Add add_3 (.a(A2_out), .b(B2_out), .c_i(add_2_c_o), .s(add_3_s), .c_o(add_3_c_o));
  Add add_4 (.a(A3_out), .b(B3_out), .c_i(add_3_c_o), .s(add_4_s), .c_o(add_4_c_o));
  not not_1 (not_1_out, add_3_s);
  not not_2 (not_2_out, add_4_s);
  not not_3 (not_3_out, add_4_s);
  not not_4 (not_4_out, add_3_s);
  not not_5 (not_5_out, add_4_s);
  not not_6 (not_6_out, add_1_s);
  not not_7 (not_7_out, add_2_s);
  not not_8 (not_8_out, add_3_s);
  not not_9 (not_9_out, add_3_s);
  not not_10 (not_10_out, add_3_s);
  not not_11 (not_11_out, add_2_s);
  not not_12 (not_12_out, add_1_s);
  not not_13 (not_13_out, add_2_s);
  not not_14 (not_14_out, add_1_s);
  not not_15 (not_15_out, add_3_s);
  not not_16 (not_16_out, add_1_s);
  not not_17 (not_17_out, add_2_s);
  not not_18 (not_18_out, add_4_s);
  not not_19 (not_19_out, add_2_s);
  not not_20 (not_20_out, add_4_s);
  not not_21 (not_21_out, add_1_s);
  not not_22 (not_22_out, add_3_s);
  not not_23 (not_23_out, add_4_s);
  and and_1 (and_1_out, add_4_s, add_3_s);
  and and_2 (and_2_out, add_4_s, not_1_out);
  and and_3 (and_3_out, not_2_out, add_3_s);
  and and_4 (and_4_out, not_3_out, not_4_out);
  and and_5 (and_5_out, not_5_out, add_2_s);
  and and_6 (and_6_out, add_4_s, not_6_out);
  and and_7 (and_7_out, add_3_s, not_7_out);
  and and_8 (and_8_out, not_8_out, add_2_s);
  and and_9 (and_9_out, not_9_out, add_1_s);
  and and_10 (and_10_out, not_10_out, not_11_out);
  and and_11 (and_11_out, add_2_s, not_12_out);
  and and_12 (and_12_out, not_13_out, not_14_out);
  and and_13 (and_13_out, not_15_out, not_16_out);
  and and_14 (and_14_out, add_3_s, not_17_out, add_1_s);
  and and_15 (and_15_out, not_18_out, add_3_s, not_19_out);
  and and_16 (and_16_out, not_20_out, add_3_s, not_21_out);
  and and_17 (and_17_out, add_4_s, not_22_out, add_2_s);
  and and_18 (and_18_out, not_23_out, add_2_s, add_1_s);
  or or_1 (or_1_out, and_13_out, and_2_out, and_5_out, and_11_out, and_14_out);
  or or_2 (or_2_out, and_1_out, and_4_out, and_10_out, and_12_out, and_18_out);
  not not_24 (not_24_out, add_2_s);
  or or_3 (or_3_out, add_1_s, not_24_out, and_3_out, and_2_out);
  or or_4 (or_4_out, and_8_out, and_13_out, and_11_out, and_14_out);
  or or_5 (or_5_out, and_13_out, and_11_out);
  or or_6 (or_6_out, and_12_out, and_15_out, and_16_out, and_17_out);
  or or_7 (or_7_out, and_6_out, and_7_out, and_11_out, and_8_out);
  Seven_Seg seven_seg_1 (
    .a(or_1_out), .b(or_2_out), .c(or_3_out), .d(or_4_out), .e(or_5_out), .f(or_6_out), .g(or_7_out),
    .dp(1'b0));
  LED led_1 (.in(add_4_s));
endmodule
