// Digital circuit zeynep_yildiz_lab2.dig as structural Verilog
module zeynep_yildiz_lab2 (
  input  in_1,
  input  in_2
);

  wire A0_out, A1_out, A2_out, add_1_c_o, add_1_s, add_2_c_o, add_2_s, add_3_c_o, add_3_s, and_1_out,
       and_2_out, and_3_out, and_4_out, and_5_out, and_6_out, and_7_out, B0_out, B1_out, B2_out, not_1_out,
       not_2_out, not_3_out, not_4_out, not_5_out, not_6_out, not_7_out, not_8_out, not_9_out, not_10_out,
       or_1_out, or_2_out, or_3_out, or_4_out;

  DipSwitch A0 (.out(A0_out));
  DipSwitch B0 (.out(B0_out));
  DipSwitch A1 (.out(A1_out));
  DipSwitch B1 (.out(B1_out));
  DipSwitch A2 (.out(A2_out));
  DipSwitch B2 (.out(B2_out));
  Add add_1 (.a(A0_out), .b(B0_out), .c_i(in_1), .s(add_1_s), .c_o(add_1_c_o));
  Add add_2 (.a(A1_out), .b(B1_out), .c_i(add_1_c_o), .s(add_2_s), .c_o(add_2_c_o));
  Add add_3 (.a(A2_out), .b(B2_out), .c_i(add_2_c_o), .s(add_3_s), .c_o(add_3_c_o));
  not not_1 (not_1_out, add_1_s);
  not not_2 (not_2_out, add_2_s);
  not not_3 (not_3_out, add_1_s);
  not not_4 (not_4_out, add_3_s);
  not not_5 (not_5_out, add_2_s);
  not not_6 (not_6_out, add_1_s);
  not not_7 (not_7_out, add_2_s);
  not not_8 (not_8_out, add_3_s);
  not not_9 (not_9_out, add_2_s);
  not not_10 (not_10_out, add_1_s);
  and and_1 (and_1_out, not_1_out, add_2_s);
  and and_2 (and_2_out, not_2_out, not_3_out);
  and and_3 (and_3_out, not_4_out, add_2_s);
  and and_4 (and_4_out, add_3_s, not_5_out);
  and and_5 (and_5_out, add_3_s, add_2_s, not_6_out);
  and and_6 (and_6_out, add_3_s, not_7_out, add_1_s);
  and and_7 (and_7_out, not_8_out, not_9_out, not_10_out);
  or or_1 (or_1_out, and_1_out, and_3_out, and_6_out, and_7_out);
  or or_2 (or_2_out, add_1_s, and_2_out);
  or or_3 (or_3_out, and_1_out, and_7_out);
  or or_4 (or_4_out, and_4_out, and_3_out, and_5_out);
  Seven_Seg seven_seg_1 (
    .a(or_1_out), .b(in_2), .c(or_2_out), .d(or_1_out), .e(or_3_out), .f(and_2_out), .g(or_4_out), .dp(1'b0));
  LED led_1 (.in(add_3_s));
endmodule
